// Logisim project ALU.circ as structural Verilog: 3 circuits, main circuit ALU
module ALU (
  input  [31:0] X,
  input  [31:0] Y,
  input  [3:0] AluOP,
  output Signed_Overflow,
  output UnSigned_Overflow,
  output Equal,
  output [31:0] Result,
  output [31:0] Result_2
);

  wire adder_1_cout, and_1_out, and_2_out, and_3_out, and_4_out, comparator_1_lt, comparator_2_lt, not_1_out,
       not_2_out, not_3_out, not_4_out, not_5_out, or_2_out, or_3_out;
  wire [31:0] adder_1_out, adder_2_out, and_5_out, bit_extender_1_out, bit_extender_2_out, divider_1_out,
       divider_1_rem, multiplier_1_cout, multiplier_1_out, negator_1_out, nor_1_out, or_1_out, shifter_1_out,
       shifter_2_out, shifter_3_out, xor_1_out;

  // Probe on X
  // Probe on X
  // Probe on Y
  // Probe on Y
  not not_1 (not_1_out, Y[31]);
  not not_2 (not_2_out, X[31]);
  not not_3 (not_3_out, negator_1_out[31]);
  Negator #(.width(32)) negator_1 (.in(Y), .out(negator_1_out));
  // Probe on AluOP
  not not_4 (not_4_out, adder_2_out[31]);
  not not_5 (not_5_out, adder_1_out[31]);
  and and_1 (and_1_out, adder_1_out[31], not_2_out, not_1_out);
  and and_2 (and_2_out, not_5_out, X[31], Y[31]);
  and and_3 (and_3_out, adder_2_out[31], not_3_out, not_2_out);
  and and_4 (and_4_out, X[31], negator_1_out[31], not_4_out);
  // Probe on Result
  // Probe on Result
  Shifter #(.width(32)) shifter_1 (.in(X), .\dist (Y[4:0]), .out(shifter_1_out));
  Shifter #(.width(32), .shift("ar")) shifter_2 (.in(X), .\dist (Y[4:0]), .out(shifter_2_out));
  Shifter #(.width(32), .shift("lr")) shifter_3 (.in(X), .\dist (Y[4:0]), .out(shifter_3_out));
  Multiplier #(.width(32)) multiplier_1 (.a(X), .b(Y), .out(multiplier_1_out), .cout(multiplier_1_cout));  // open: cin
  Divider #(.width(32)) divider_1 (.a(X), .b(Y), .out(divider_1_out), .rem(divider_1_rem));  // open: upper
  Adder #(.width(32)) adder_1 (.a(X), .b(Y), .out(adder_1_out), .cout(adder_1_cout));  // open: cin
  Adder #(.width(32)) adder_2 (.a(X), .b(negator_1_out), .out(adder_2_out));  // open: cin, cout
  assign and_5_out = X & Y;  // AND_Gate and_5, 32 bits wide
  assign or_1_out = X | Y;  // OR_Gate or_1, 32 bits wide
  assign xor_1_out = X ^ Y;  // XOR_Gate xor_1, 32 bits wide
  assign nor_1_out = ~(X | Y);  // NOR_Gate nor_1, 32 bits wide
  Comparator #(.width(32)) comparator_1 (.a(X), .b(Y), .lt(comparator_1_lt));  // open: gt, eq
  Comparator #(.width(32), .mode("unsigned")) comparator_2 (
    .a(X), .b(Y), .eq(Equal), .lt(comparator_2_lt));  // open: gt
  assign bit_extender_1_out = {{31{1'b0}}, comparator_1_lt};  // Bit_Extender bit_extender_1
  assign bit_extender_2_out = {{31{1'b0}}, comparator_2_lt};  // Bit_Extender bit_extender_2
  // Probe on Result_2
  Multiplexer #(.select(4), .width(32)) multiplexer_1 (
    .in0(shifter_1_out), .in1(shifter_2_out), .in2(shifter_3_out), .in3(multiplier_1_out),
    .in4(divider_1_out), .in5(adder_1_out), .in6(adder_2_out), .in7(and_5_out), .in8(or_1_out),
    .in9(xor_1_out), .in10(nor_1_out), .in11(bit_extender_1_out), .in12(bit_extender_2_out), .out(Result),
    .sel(AluOP));  // open: in13, in14, in15, en
  or or_2 (or_2_out, and_1_out, and_2_out);
  or or_3 (or_3_out, and_3_out, and_4_out);
  Multiplexer #(.select(4), .width(32)) multiplexer_2 (
    .in0({32{1'b0}}), .in1({32{1'b0}}), .in2({32{1'b0}}), .in3(multiplier_1_cout), .in4(divider_1_rem),
    .in5({32{1'b0}}), .in6({32{1'b0}}), .in7({32{1'b0}}), .in8({32{1'b0}}), .in9({32{1'b0}}),
    .in10({32{1'b0}}), .in11({32{1'b0}}), .in12({32{1'b0}}), .in13({32{1'b0}}), .in14({32{1'b0}}),
    .in15({32{1'b0}}), .out(Result_2), .sel(AluOP));  // open: en
  Multiplexer #(.select(4)) multiplexer_3 (
    .in0(1'b0), .in1(1'b0), .in2(1'b0), .in3(1'b0), .in4(1'b0), .in5(adder_1_cout), .in6(comparator_2_lt),
    .in7(1'b0), .in8(1'b0), .in9(1'b0), .in10(1'b0), .in11(1'b0), .in12(1'b0), .in13(1'b0), .in14(1'b0),
    .in15(1'b0), .out(UnSigned_Overflow), .sel(AluOP));  // open: en
  Multiplexer #(.select(4)) multiplexer_4 (
    .in0(1'b0), .in1(1'b0), .in2(1'b0), .in3(1'b0), .in4(1'b0), .in5(or_2_out), .in6(or_3_out), .in7(1'b0),
    .in8(1'b0), .in9(1'b0), .in10(1'b0), .in11(1'b0), .in12(1'b0), .in13(1'b0), .in14(1'b0), .in15(1'b0),
    .out(Signed_Overflow), .sel(AluOP));  // open: en

  // Other names for the same wires on the sheet: OF = Signed_Overflow; Result2[31:0] = Result_2; S[3:0] = AluOP;
  //   UOF = UnSigned_Overflow

  // Notes on the sheet:
  //   不要改变此引脚区域内容，也不要改变ALU封装形式
  //   输入引脚
  //   请在下方利用上方输入输出引脚的隧道信号构建ALU电路，ctrl+d复制选择部件
  //   华中科技大学计算机学院 计算机组成原理，鸣谢加州大学伯克利CS61C课程
  //   输出引脚
  //   探测区域
endmodule

module test (
  output Signed_Overflow,
  output Unsigned_overflow,
  output [31:0] Result,
  output Equal,
  output [31:0] Result_2
);

  wire clock_1_out;
  wire [3:0] rom_3_data;
  wire [7:0] adder_1_out, register_1_q;
  wire [31:0] rom_1_data, rom_2_data;

  Clock clock_1 (.out(clock_1_out));
  Adder adder_1 (.a(8'h1), .b(register_1_q), .out(adder_1_out));  // open: cin, cout
  Register register_1 (.D(adder_1_out), .Q(register_1_q), .clk(clock_1_out));  // open: en, clr
  // Probe on register_1_q
  // Probe on rom_1_data
  ROM #(.dataWidth(32)) rom_1 (.addr(register_1_q), .data(rom_1_data));  // open: sel
  ROM #(.dataWidth(32)) rom_2 (.addr(register_1_q), .data(rom_2_data));  // open: sel
  // Probe on rom_2_data
  ROM #(.dataWidth(4)) rom_3 (.addr(register_1_q), .data(rom_3_data));  // open: sel
  ALU alu_1 (
    .AluOP(rom_3_data), .X(rom_1_data), .Equal(Equal), .Result(Result), .Signed_Overflow(Signed_Overflow),
    .Y(rom_2_data), .Result_2(Result_2), .UnSigned_Overflow(Unsigned_overflow));
  // Probe on Result
  // Probe on Result_2

  // Notes on the sheet:
  //   此电路用于检测学生设计的ALU部件封装是否符合要求
  //   当电路设计完成后，蓝色线红色不应该出现，输出也不应该是高阻态
  //   ROM中可以存放测试用例，使用时钟驱动调出不同的X，Y，S值进行批量验证
  //   封装的ALU应该正好放置于此
endmodule

module four_bits_adder (
  input  [3:0] in_1,
  input  in_2,
  input  [3:0] in_3,
  input  [3:0] in_4,
  output C0,
  output C1,
  output C2,
  output C3
);

  wire and_1_out, and_2_out, and_3_out, G1_out, G2_out, G3_out, P1_out, P1C0_out, P2_out, P2G1_out,
       P2P1C0_out, P3_out, P3G2_out, P3P2G1_out, P3P2P1C0_out, xor_1_out, xor_2_out, xor_3_out, xor_4_out;

  and and_1 (and_1_out, in_2, in_4[0]);
  and and_2 (and_2_out, in_2, in_3[0]);
  and and_3 (and_3_out, in_4[0], in_3[0]);
  and G2 (G2_out, in_4[2], in_3[2]);
  and G3 (G3_out, in_4[3], in_3[3]);
  xor P3 (P3_out, in_4[3], in_3[3]);
  or u_C0 (C0, and_1_out, and_2_out, and_3_out);
  and G1 (G1_out, in_4[1], in_3[1]);
  xor P1 (P1_out, in_4[1], in_3[1]);
  xor P2 (P2_out, in_4[2], in_3[2]);
  and P1C0 (P1C0_out, C0, P1_out);
  and P2P1C0 (P2P1C0_out, P1_out, C0, P2_out);
  and P2G1 (P2G1_out, G1_out, P2_out);
  and P3P2G1 (P3P2G1_out, G1_out, P2_out, P3_out);
  and P3G2 (P3G2_out, G2_out, P3_out);
  or u_C1 (C1, P1C0_out, G1_out);
  or u_C2 (C2, P2P1C0_out, G2_out, P2G1_out);
  and P3P2P1C0 (P3P2P1C0_out, C0, P1_out, P2_out, P3_out);
  ExactlyOne xor_1 (.out(xor_1_out), .in0(in_4[0]), .in1(in_2), .in2(in_3[0]));
  ExactlyOne xor_2 (.out(xor_2_out), .in0(in_4[1]), .in1(C1), .in2(in_3[1]));
  ExactlyOne xor_3 (.out(xor_3_out), .in0(in_4[2]), .in1(C2), .in2(in_3[2]));
  or C2_2 (C3, G3_out, P3P2G1_out, P3G2_out, P3P2P1C0_out);
  ExactlyOne xor_4 (.out(xor_4_out), .in0(in_4[3]), .in1(C3), .in2(in_3[3]));

  // Other names for the same wires on the sheet: C = in_2; X[3:0] = in_4; Y[3:0] = in_3; Z[3:0] = in_1
endmodule
