// Logisim project cpu_complete.circ as structural Verilog: 12 circuits, main circuit main
module main (
);

  wire _1_out, _2_out, _3_out, alu_4_equal, and_2_out, and_3_out, bit_extender_6_out, clock, clock_1_out,
       comparator_1_eq, controller_1_bgez, controller_1_cpr0, controller_1_eret, controller_1_lbu,
       controller_1_mfc0, controller_1_oporfun, controller_1_shift, controller_1_shift_op_judge,
       controller_1_syscall, controller_1_we, cp0, ex_eret, EX_int_tri, ex_mtc0, EXl, EXMEM_jal_2,
       EXMEM_lbu_2, EXMEM_syscall_2, EXMEM_we_2, ID_mtc0, IDEX_bgez_2, IDEX_lbu_2, IDEX_syscall_2, IDEX_we_2,
       ifid_1_int_sig, interrupt_1_p12, interrupt_1_p15, jal, jump, lock, memwb_1_ld_2, memwb_1_we_2, mfc0,
       multiplexer_10_out, multiplexer_12_out, nand_1_out, not_1_out, not_2_out, not_3_out, not_4_out,
       syscall, undriven, undriven_2, undriven_3, xor_1_out;
  wire [0:0] IDEX_mem_label_2;
  wire [1:0] controller_1_b_ins_label, controller_1_j_label, controller_1_mem_label, EX_int_num,
       EXMEM_mem_label_2, IDEX_b_ins_out, IDEX_jump_2, ifid_1_int_num_out, interrupt_1_p11, Red_R1, Red_R2;
  wire [3:0] controller_1_aluop, IDEX_aluop_2;
  wire [4:0] bit_extender_4_out, controller_1_r1_sel, controller_1_r2_sel, controller_1_rw, EXMEM_rw_2,
       IDEX_rw_2, memwb_1_rw_2;
  wire [7:0] multiplexer_18_out, ram_1_data, ram_1_data_2, ram_1_data_3, ram_1_data_4;
  wire [9:0] bit_extender_3_out, multiplexer_1_out, PC_jump, PC_q;
  wire [11:0] bit_extender_8_out;
  wire [14:0] counter_1_q, counter_2_q, counter_3_q;
  wire [31:0] a0, alu_2_result, alu_3_result, bit_extender_1_out, bit_extender_2_out, bit_extender_5_out,
       bit_extender_7_out, bit_extender_10_out, controller_1_cpr_value, controller_1_imm16_ext,
       controller_1_instr_index, controller_1_shamt_ext, cp0_value, EPC_va, ex_pc_next, ex_redir, EX_rt,
       EXMEM_pc_2, EXMEM_ram_write, EXMEM_result_2, IDEX_imm16_out, IDEX_jal_addr_out, IDEX_x, IDEX_y,
       ifid_1_epc_out, ifid_1_ie_out, ifid_1_instruction_out, ifid_1_pc_out, interrupt_1_p14, ld_redir,
       main_1_reg1, main_1_reg2_2, main_1_s0_value, mem_redir, memwb_1_sel1_2, memwb_1_sel2_2,
       multiplexer_2_out, multiplexer_3_out, multiplexer_4_out, multiplexer_5_out, multiplexer_6_out,
       multiplexer_7_out, multiplexer_8_out, multiplexer_9_out, multiplexer_11_out, multiplexer_13_out,
       multiplexer_14_out, multiplexer_15_out, multiplexer_16_out, multiplexer_17_out, PC_4, PC_jal,
       register_1_q, rom_1_data, v0;

  Multiplexer #(.width(10), .enable("false")) multiplexer_1 (
    .in0(bit_extender_3_out), .in1(PC_jump), .out(multiplexer_1_out), .sel(jump));
  not not_1 (not_1_out, lock);
  // Probe on counter_1_q
  Counter #(.width(15), .max('h7fff)) counter_1 (.Q(counter_1_q), .clk(lock));  // open: load, D, count, carry, clr
  Hex_Digit_Display hex_digit_display_1 (.value(multiplexer_2_out[31:28]));  // open: dp
  assign bit_extender_1_out = {{29{1'b0}}, 3'b001};  // Bit_Extender bit_extender_1
  Register #(.width(10)) PC (.D(multiplexer_1_out), .en(not_1_out), .Q(PC_q), .clk(clock));  // open: clr
  Hex_Digit_Display hex_digit_display_2 (.value(multiplexer_2_out[23:20]));  // open: dp
  Hex_Digit_Display hex_digit_display_3 (.value(multiplexer_2_out[27:24]));  // open: dp
  Multiplexer #(.width(32), .enable("false")) multiplexer_2 (
    .in0({32{1'b0}}), .in1(a0), .out(multiplexer_2_out), .sel(nand_1_out));
  assign bit_extender_2_out = {{22{1'b0}}, PC_q};  // Bit_Extender bit_extender_2
  Button _1 (.out(_1_out));
  Button _2 (.out(_2_out));
  Button _3 (.out(_3_out));
  // Probe on Red_R1
  // Probe on Red_R2
  Hex_Digit_Display hex_digit_display_4 (.value(multiplexer_2_out[15:12]));  // open: dp
  Hex_Digit_Display hex_digit_display_5 (.value(multiplexer_2_out[19:16]));  // open: dp
  Bit_Extender #(.in_width(32), .out_width(10)) bit_extender_3 (.in(PC_4), .out(bit_extender_3_out));
  ALU alu_1 (
    .AluOP(4'b0101), .X(bit_extender_1_out), .Result(PC_4), .Y(bit_extender_2_out));  // open: Equal, Signed_Overflow, Result_2, UnSigned_Overflow
  ROM #(.addrWidth(10), .dataWidth(32)) rom_1 (.addr(PC_q), .data(rom_1_data), .sel(1'b1));
  // interrupt interrupt_1: pin names not known; wires that end beside it: _1_out, _2_out, _3_out, ex_mtc0, EX_int_tri, ex_eret, ex_pc_next, EX_rt, cp0, clock, interrupt_1_p11, interrupt_1_p12, EPC_va, interrupt_1_p14, interrupt_1_p15
  // Probe on mem_redir
  // Probe on ex_redir
  Hex_Digit_Display hex_digit_display_6 (.value(multiplexer_2_out[11:8]));  // open: dp
  Comparator #(.width(32), .mode("unsigned")) comparator_1 (.a(v0), .b(32'ha), .eq(comparator_1_eq));  // open: gt, lt
  // Probe on alu_2_result
  ALU alu_2 (
    .AluOP(4'b0000), .X(bit_extender_2_out), .Result(alu_2_result), .Y(32'h2));  // open: Equal, Signed_Overflow, Result_2, UnSigned_Overflow
  IFID ifid_1 (
    .PC_1(PC_4), .instruction(rom_1_data), .clk(clock), .PC_out(ifid_1_pc_out),
    .instruction_out(ifid_1_instruction_out), .rst(jump), .lock(lock), .IE(interrupt_1_p14), .EPC(EPC_va),
    .int_trigger(interrupt_1_p12), .which_int(interrupt_1_p11), .IE_out(ifid_1_ie_out),
    .EPC_out(ifid_1_epc_out), .int_sig(ifid_1_int_sig), .int_num_out(ifid_1_int_num_out));
  // Probe on interrupt_1_p14
  // Probe on interrupt_1_p15
  Hex_Digit_Display hex_digit_display_7 (.value(multiplexer_2_out[3:0]));  // open: dp
  Hex_Digit_Display hex_digit_display_8 (.value(multiplexer_2_out[7:4]));  // open: dp
  and and_1 (clock, clock_1_out, nand_1_out);
  nand nand_1 (nand_1_out, comparator_1_eq, syscall);
  and and_2 (and_2_out, controller_1_shift_op_judge, controller_1_shift);
  Clock clock_1 (.out(clock_1_out));
  Controller controller_1 (
    .instruction(ifid_1_instruction_out), .instr_index(controller_1_instr_index),
    .imm16_ext(controller_1_imm16_ext), .shamt_ext(controller_1_shamt_ext),
    .b_ins_label(controller_1_b_ins_label), .aluop(controller_1_aluop), .OporFun(controller_1_oporfun),
    .R1_sel(controller_1_r1_sel), .mem_label(controller_1_mem_label), .RW(controller_1_rw),
    .We(controller_1_we), .R2_sel(controller_1_r2_sel), .syscall(controller_1_syscall),
    .bgez(controller_1_bgez), .shift(controller_1_shift), .lbu(controller_1_lbu),
    .shift_op_judge(controller_1_shift_op_judge), .j_label(controller_1_j_label), .mfc0(controller_1_mfc0),
    .mtc0(ID_mtc0), .IE_value(ifid_1_ie_out), .EPC_value(ifid_1_epc_out), .CPR_value(controller_1_cpr_value),
    .CPR0(controller_1_cpr0), .eret(controller_1_eret));
  Counter #(.width(15), .max('h7fff)) counter_2 (.Q(counter_2_q), .clk(clock));  // open: load, D, count, carry, clr
  Multiplexer #(.width(32), .enable("false")) multiplexer_3 (
    .in0(multiplexer_4_out), .in1(controller_1_instr_index), .out(multiplexer_3_out),
    .sel(controller_1_oporfun));
  // Probe on main_1_s0_value
  regfile_v0_main main_1 (
    .Reg1_num(controller_1_r1_sel), .Reg2(controller_1_r2_sel), .Write_Reg_num(memwb_1_rw_2),
    .Din(multiplexer_7_out), .Write_Enable(memwb_1_we_2), .Clock(not_2_out), .Reg1(main_1_reg1),
    .Reg2_2(main_1_reg2_2), .s0_Value(main_1_s0_value), .v0_Value(v0), .a0_value(a0));  // open: s1_Value
  not not_2 (not_2_out, clock);
  Redirection redirection_1 (
    .lock(lock), .EX_RW(IDEX_rw_2), .ID_R1(controller_1_r1_sel), .EX_We(IDEX_we_2),
    .ID_OporFun(controller_1_oporfun), .ID_shift(controller_1_shift), .ID_R2(controller_1_r2_sel),
    .MEM_RW(EXMEM_rw_2), .MEM_We(EXMEM_we_2), .ID_mem(controller_1_mem_label), .Red_R1(Red_R1),
    .Red_R2(Red_R2), .EX_load(EXl), .ID_mtc0(ID_mtc0));  // open: IDMEMinter
  // Probe on counter_2_q
  Multiplexer #(.select(2), .width(32), .enable("false")) multiplexer_4 (
    .in0(main_1_reg1), .in1(ex_redir), .in2(mem_redir), .in3(ex_redir), .out(multiplexer_4_out), .sel(Red_R1));
  Multiplexer #(.select(2), .width(32), .enable("false")) multiplexer_5 (
    .in0(main_1_reg2_2), .in1(ex_redir), .in2(mem_redir), .in3(ex_redir), .out(multiplexer_5_out),
    .sel(Red_R2));
  Bit_Extender #(.in_width(32), .out_width(5)) bit_extender_4 (.in(multiplexer_5_out), .out(bit_extender_4_out));
  Multiplexer #(.width(32), .enable("false")) multiplexer_6 (
    .in0(multiplexer_5_out), .in1(controller_1_imm16_ext), .out(multiplexer_6_out), .sel(controller_1_oporfun));
  assign bit_extender_5_out = {{27{1'b0}}, bit_extender_4_out};  // Bit_Extender bit_extender_5
  Multiplexer #(.width(32), .enable("false")) multiplexer_7 (
    .in0(multiplexer_15_out), .in1(PC_jal), .out(multiplexer_7_out), .sel(jal));
  // Probe on undriven
  Multiplexer #(.width(32), .enable("false")) multiplexer_8 (
    .in0(controller_1_shamt_ext), .in1(bit_extender_5_out), .out(multiplexer_8_out), .sel(and_2_out));
  IDEX IDEX (
    .PC_1(ifid_1_pc_out), .PC_out(ex_pc_next), .jal_addr(multiplexer_3_out),
    .jal_addr_out(IDEX_jal_addr_out), .imm16_ext(controller_1_imm16_ext), .imm16_out(IDEX_imm16_out),
    .b_ins_label(controller_1_b_ins_label), .b_ins_out(IDEX_b_ins_out), .X_op(multiplexer_4_out), .X(IDEX_x),
    .Y_op(multiplexer_9_out), .Y(IDEX_y), .write_value(multiplexer_5_out), .ram_write(EX_rt),
    .aluop(controller_1_aluop), .aluop_2(IDEX_aluop_2), .mem_label(controller_1_mem_label),
    .mem_label_2({EXl, IDEX_mem_label_2[0]}), .lbu(controller_1_lbu), .lbu_2(IDEX_lbu_2),
    .jump(controller_1_j_label), .jump_2(IDEX_jump_2), .bgez(controller_1_bgez), .bgez_2(IDEX_bgez_2),
    .clk(clock), .Rw(controller_1_rw), .Rw_2(IDEX_rw_2), .we(controller_1_we), .we_2(IDEX_we_2),
    .syscall(controller_1_syscall), .syscall_2(IDEX_syscall_2), .reset(jump), .nop(multiplexer_10_out),
    .CPR0(controller_1_cpr0), .CPR0_2(cp0), .CPR0_value(controller_1_cpr_value), .CPR0_value_2(cp0_value),
    .mfc0(controller_1_mfc0), .mfc0_2(mfc0), .mtc0(ID_mtc0), .mtc0_2(ex_mtc0), .int_trigger(ifid_1_int_sig),
    .int_trigger_2(EX_int_tri), .int_num(ifid_1_int_num_out), .int_num_out(EX_int_num),
    .eret(controller_1_eret), .eret_2(ex_eret));
  Multiplexer #(.width(32), .enable("false")) multiplexer_9 (
    .in0(multiplexer_6_out), .in1(multiplexer_8_out), .out(multiplexer_9_out), .sel(controller_1_shift));
  Multiplexer #(.enable("false")) multiplexer_10 (.in0(1'b0), .in1(1'b1), .out(multiplexer_10_out), .sel(lock));
  Register #(.width(32), .trigger("falling")) register_1 (
    .D(ex_pc_next), .en(jump), .Q(register_1_q), .clk(not_3_out));  // open: clr
  not not_3 (not_3_out, clock);
  ALU alu_3 (
    .AluOP(4'b0101), .X(ex_pc_next), .Result(alu_3_result), .Y(IDEX_imm16_out));  // open: Equal, Signed_Overflow, Result_2, UnSigned_Overflow
  // Probe on register_1_q
  and and_3 (and_3_out, IDEX_b_ins_out[1], xor_1_out);
  not not_4 (not_4_out, IDEX_b_ins_out[0]);
  // Probe on undriven_2
  ALU alu_4 (
    .AluOP(IDEX_aluop_2), .X(IDEX_x), .Equal(alu_4_equal), .Result(ex_redir), .Y(IDEX_y));  // open: Signed_Overflow, Result_2, UnSigned_Overflow
  Multiplexer #(.width(32), .enable("false")) multiplexer_11 (
    .in0(ex_pc_next), .in1(alu_3_result), .out(multiplexer_11_out), .sel(and_3_out));
  or or_1 (jump, and_3_out, EX_int_tri, IDEX_jump_2[0], ex_eret);
  Multiplexer #(.enable("false")) multiplexer_12 (
    .in0(alu_4_equal), .in1(bit_extender_6_out), .out(multiplexer_12_out), .sel(IDEX_bgez_2));
  xor xor_1 (xor_1_out, not_4_out, multiplexer_12_out);
  Bit_Extender #(.in_width(32), .out_width(1)) bit_extender_6 (.in(ex_redir), .out(bit_extender_6_out));
  Multiplexer #(.width(32), .enable("false")) multiplexer_13 (
    .in0(multiplexer_11_out), .in1(IDEX_jal_addr_out), .out(multiplexer_13_out), .sel(IDEX_jump_2[0]));
  EXMEM EXMEM (
    .result(multiplexer_14_out), .result_2(EXMEM_result_2), .write_value(EX_rt), .ram_write(EXMEM_ram_write),
    .mem_label({EXl, IDEX_mem_label_2[0]}), .mem_label_2(EXMEM_mem_label_2), .lbu(IDEX_lbu_2),
    .lbu_2(EXMEM_lbu_2), .clk(clock), .PC(ex_pc_next), .PC_2(EXMEM_pc_2), .Rw(IDEX_rw_2), .Rw_2(EXMEM_rw_2),
    .we(IDEX_we_2), .we_2(EXMEM_we_2), .syscall(IDEX_syscall_2), .syscall_2(EXMEM_syscall_2),
    .jal(IDEX_jump_2[1]), .jal_2(EXMEM_jal_2));
  Multiplexer #(.width(32), .enable("false")) multiplexer_14 (
    .in0(ex_redir), .in1(cp0_value), .out(multiplexer_14_out), .sel(mfc0));
  Counter #(.width(15), .max('h7fff)) counter_3 (
    .count(jump), .Q(counter_3_q), .clk(clock));  // open: load, D, carry, clr
  // Probe on counter_3_q
  // Probe on ex_pc_next
  Multiplexer #(.width(32), .enable("false")) multiplexer_15 (
    .in0(memwb_1_sel1_2), .in1(memwb_1_sel2_2), .out(multiplexer_15_out), .sel(memwb_1_ld_2));
  Multiplexer #(.width(32), .enable("false")) multiplexer_16 (
    .in0(multiplexer_13_out), .in1(bit_extender_7_out), .out(multiplexer_16_out), .sel(EX_int_tri));
  assign bit_extender_7_out = {{30{1'b0}}, EX_int_num};  // Bit_Extender bit_extender_7
  // Probe on undriven_3
  Bit_Extender #(.in_width(32), .out_width(12)) bit_extender_8 (.in(EXMEM_result_2), .out(bit_extender_8_out));
  Multiplexer #(.width(32), .enable("false")) multiplexer_17 (
    .in0(multiplexer_16_out), .in1(EPC_va), .out(multiplexer_17_out), .sel(ex_eret));
  Bit_Extender #(.in_width(32), .out_width(10)) bit_extender_9 (.in(multiplexer_17_out), .out(PC_jump));
  RAM #(.addrWidth(10), .dataWidth(32), .bus("separate")) ram_1 (
    .addr(bit_extender_8_out[11:2]), .din(EXMEM_ram_write),
    .data({ram_1_data_4, ram_1_data_3, ram_1_data_2, ram_1_data}), .str(EXMEM_mem_label_2[0]), .sel(1'b1),
    .clk(clock), .ld(EXMEM_mem_label_2[1]));  // open: clr
  // Probe on memwb_1_rw_2
  Multiplexer #(.select(2), .width(8), .enable("false")) multiplexer_18 (
    .in0(ram_1_data), .in1(ram_1_data_2), .in2(ram_1_data_3), .in3(ram_1_data_4), .out(multiplexer_18_out),
    .sel(bit_extender_8_out[1:0]));
  Multiplexer #(.width(32), .enable("false")) multiplexer_19 (
    .in0(EXMEM_result_2), .in1(ld_redir), .out(mem_redir), .sel(EXMEM_mem_label_2[1]));
  MEMWB memwb_1 (
    .sel1(EXMEM_result_2), .sel2(ld_redir), .clk(clock), .sel1_2(memwb_1_sel1_2), .sel2_2(memwb_1_sel2_2),
    .ld(EXMEM_mem_label_2[1]), .ld_2(memwb_1_ld_2), .Rw(EXMEM_rw_2), .Rw_2(memwb_1_rw_2), .we(EXMEM_we_2),
    .we_2(memwb_1_we_2), .syscall(EXMEM_syscall_2), .syscall_2(syscall), .PC_jal(EXMEM_pc_2),
    .PC_jal_2(PC_jal), .jal(EXMEM_jal_2), .jal_2(jal));
  assign bit_extender_10_out = {{24{1'b0}}, multiplexer_18_out};  // Bit_Extender bit_extender_10
  Multiplexer #(.width(32), .enable("false")) multiplexer_20 (
    .in0({ram_1_data_4, ram_1_data_3, ram_1_data_2, ram_1_data}), .in1(bit_extender_10_out), .out(ld_redir),
    .sel(EXMEM_lbu_2));
  // Probe on ld_redir

  // Notes on the sheet:
  //   contents of rom_1 (hex, n*v repeats v):
  //   8000c04 8000ce0 8000d24 8000d4f 201d00c8 20110001 8000c0a 20110001 20120002 20130003 8000c0e
  //   20110001 20120002 20130003 8000c12 20110001 20120002 20130003 8000c16 20110001 20120002 20130003
  //   c000cbd 20100001 20110001 118fc0 112020 20020022 c 118882 12200001 8000c1a 112020 20020022 c
  //   20110001 118880 112020 20020022 c 12200001 8000c24 20110001 118fc0 112020 20020022 c 1188c3 112020
  //   20020022 c 118903 112020 20020022 c 118903 112020 20020022 c 118903 112020 20020022 c 118903 112020
  //   20020022 c 118903 112020 20020022 c 118903 112020 20020022 c 118903 112020 20020022 c 20100001
  //   109fc0 139fc3 8021 2012000c 24160003 26100001 3210000f 20080008 20090001 139900 2709825 132020
  //   20020022 c 1094022 1500fff9 22100001 2018000f 2188024 108700 20080008 20090001 139902 2709825 132021
  //   20020022 c 1094022 1500fff9 108702 2c9b022 12c00001 8000c55 4020 1084027 84400 3508ffff 82021
  //   20020022 c 2010ffff 20110000 ae300000 22100001 22310004 ae300000 22100001 22310004 ae300000 22100001
  //   22310004 ae300000 22100001 22310004 ae300000 22100001 22310004 ae300000 22100001 22310004 ae300000
  //   22100001 22310004 ae300000 22100001 22310004 ae300000 22100001 22310004 ae300000 22100001 22310004
  //   ae300000 22100001 22310004 ae300000 22100001 22310004 ae300000 22100001 22310004 ae300000 22100001
  //   22310004 ae300000 22100001 22310004 ae300000 22100001 22310004 22100001 8020 2011003c 8e130000
  //   8e340000 274402a 11000002 ae330000 ae140000 2231fffc 1611fff8 102020 20020022 c 22100004 2011003c
  //   1611fff2 2002000a c 20100000 22100001 102020 20020022 c 22100002 102020 20020022 c 22100003 102020
  //   20020022 c 22100004 102020 20020022 c 22100005 102020 20020022 c 22100006 102020 20020022 c 22100007
  //   102020 20020022 c 22100008 102020 20020022 20020022 c 3e00008 201b0001 409b0000 401b0800 afb00000
  //   afb1fffc afb2fff8 afb3fff4 afa4fff0 afbbffec 23bdffe8 201b0000 409b0000 20100007 20110000 20120004
  //   118900 22310001 22240000 2210ffff 601fffb 20100007 2518806 22240000 2210ffff 601fffc 20100007
  //   2013001c 2e510004 22330000 22640000 2e510005 22330000 22640000 2210ffff 601fff8 20100013 108200
  //   22100012 108200 22100011 108200 22100010 201100d0 ae300000 92300000 22040000 92300001 22040000
  //   92300002 22040000 92300003 22040000 201b0001 409b0000 8fbb0004 8fa40008 8fb3000c 8fb20010 8fb10014
  //   409b0800 8fb00018 23bd0018 201b0000 409b0000 0 0 0 42000018 201b0001 409b0000 401b0800 afb00000
  //   afb1fffc afb2fff8 afb3fff4 afa4fff0 afbbffec 23bdffe8 201b0000 409b0000 20100007 20110000 20120004
  //   118900 22310002 22240000 2210ffff 601fffb 20100007 2518806 22240000 2210ffff 601fffc 20100007
  //   2013001c 201b0001 409b0000 8fbb0004 8fa40008 8fb3000c 8fb20010 8fb10014 409b0800 8fb00018 23bd0018
  //   201b0000 409b0000 0 0 0 42000018 201b0001 409b0000 401b0800 afb00000 afb1fffc afb2fff8 afb3fff4
  //   afa4fff0 afbbffec 23bdffe8 201b0000 409b0000 20100007 20110000 20120004 118900 22310003 22240000
  //   2210ffff 601fffb 20100007 2518806 22240000 2210ffff 601fffc 20100007 2013001c 201b0001 409b0000
  //   8fbb0004 8fa40008 8fb3000c 8fb20010 8fb10014 409b0800 8fb00018 23bd0018 201b0000 409b0000 0 0 0
  //   42000018
endmodule

module IR (
  input  [31:0] \input ,
  output [25:0] _25_0,
  output [5:0] _26_31,
  output [4:0] _21_25,
  output [4:0] _16_20,
  output [4:0] _11_15,
  output [15:0] _0_15,
  output [5:0] _5_0,
  output [4:0] _6_10
);


  assign _0_15 = \input [15:0];
  assign _5_0 = \input [5:0];
  assign _6_10 = \input [10:6];
  assign _11_15 = \input [15:11];
  assign _16_20 = \input [20:16];
  assign _21_25 = \input [25:21];
  assign _25_0 = \input [25:0];
  assign _26_31 = \input [31:26];
endmodule

module istWithOp (
  input  i31,
  input  i30,
  input  i29,
  input  i28,
  input  i27,
  input  i26,
  output j,
  output j2,
  output op3,
  output op2,
  output op1,
  output op0,
  output rw,
  output rw2,
  output eq,
  output eq2,
  output regwrite,
  output LBU
);

  wire and_2_out, and_3_out, and_4_out, and_5_out, and_6_out, and_7_out, and_8_out, and_9_out, and_10_out,
       and_11_out, and_12_out, and_13_out, and_14_out, and_15_out, and_16_out, and_17_out, and_18_out,
       and_19_out, and_20_out, and_21_out, and_22_out, and_23_out, and_24_out, and_25_out, and_26_out,
       and_27_out, and_28_out, and_29_out, and_30_out, and_31_out, and_32_out, not_1_out, not_2_out,
       not_3_out, not_4_out, not_6_out, not_7_out, not_8_out, not_9_out, not_10_out, not_11_out, not_12_out,
       not_13_out, not_14_out, not_15_out, not_16_out, not_17_out, not_18_out, not_19_out, not_20_out,
       not_21_out, not_22_out, not_23_out, not_24_out, not_25_out, not_26_out, not_27_out, not_28_out,
       not_29_out, not_30_out, not_31_out, not_32_out, not_33_out, not_34_out, not_35_out, not_36_out,
       not_37_out, not_38_out, not_39_out, not_40_out, not_41_out, not_42_out, not_43_out, not_44_out,
       not_45_out, not_46_out, not_47_out, not_48_out, not_49_out, not_50_out, not_51_out, not_52_out,
       not_53_out, not_54_out, not_55_out, not_56_out, not_57_out, not_58_out, not_59_out, not_60_out,
       not_61_out, not_62_out, not_63_out, not_64_out, not_65_out, not_67_out, not_68_out, not_69_out,
       not_70_out, not_71_out, not_72_out, not_73_out, not_74_out, not_75_out, not_76_out, not_77_out,
       not_78_out, not_79_out, not_80_out, not_81_out, not_82_out, not_83_out;

  not not_1 (not_1_out, i31);
  not not_2 (not_2_out, i30);
  not not_3 (not_3_out, i29);
  not not_4 (not_4_out, i28);
  not not_5 (j2, i26);
  not not_6 (not_6_out, i31);
  not not_7 (not_7_out, i30);
  not not_8 (not_8_out, i29);
  not not_9 (not_9_out, i28);
  not not_10 (not_10_out, i27);
  not not_11 (not_11_out, i31);
  not not_12 (not_12_out, i30);
  not not_13 (not_13_out, i28);
  not not_14 (not_14_out, i27);
  not not_15 (not_15_out, i26);
  not not_16 (not_16_out, i31);
  not not_17 (not_17_out, i30);
  not not_18 (not_18_out, i29);
  not not_19 (not_19_out, i27);
  not not_20 (not_20_out, i30);
  not not_21 (not_21_out, i28);
  not not_22 (not_22_out, i28);
  not not_23 (not_23_out, i27);
  not not_24 (not_24_out, i30);
  not not_25 (not_25_out, i28);
  not not_26 (not_26_out, i31);
  not not_27 (not_27_out, i30);
  not not_28 (not_28_out, i29);
  not not_29 (not_29_out, i27);
  not not_30 (not_30_out, i31);
  not not_31 (not_31_out, i26);
  not not_32 (not_32_out, i26);
  not not_33 (not_33_out, i31);
  not not_34 (not_34_out, i30);
  not not_35 (not_35_out, i26);
  not not_36 (not_36_out, i26);
  not not_37 (not_37_out, i26);
  not not_38 (not_38_out, i28);
  not not_39 (not_39_out, i27);
  not not_40 (not_40_out, i31);
  not not_41 (not_41_out, i30);
  not not_42 (not_42_out, i28);
  not not_43 (not_43_out, i26);
  not not_44 (not_44_out, i27);
  not not_45 (not_45_out, i26);
  not not_46 (not_46_out, i27);
  not not_47 (not_47_out, i26);
  not not_48 (not_48_out, i27);
  not not_49 (not_49_out, i26);
  not not_50 (not_50_out, i30);
  not not_51 (not_51_out, i28);
  not not_52 (not_52_out, i30);
  not not_53 (not_53_out, i28);
  not not_54 (not_54_out, i30);
  not not_55 (not_55_out, i29);
  not not_56 (not_56_out, i27);
  not not_57 (not_57_out, i26);
  not not_58 (not_58_out, i31);
  not not_59 (not_59_out, i30);
  not not_60 (not_60_out, i29);
  not not_61 (not_61_out, i27);
  not not_62 (not_62_out, i31);
  not not_63 (not_63_out, i30);
  not not_64 (not_64_out, i29);
  not not_65 (not_65_out, i27);
  not not_66 (eq2, i26);
  not not_67 (not_67_out, i31);
  not not_68 (not_68_out, i30);
  not not_69 (not_69_out, i28);
  not not_70 (not_70_out, i31);
  not not_71 (not_71_out, i30);
  not not_72 (not_72_out, i27);
  not not_73 (not_73_out, i30);
  not not_74 (not_74_out, i29);
  not not_75 (not_75_out, i28);
  not not_76 (not_76_out, i30);
  not not_77 (not_77_out, i29);
  not not_78 (not_78_out, i27);
  not not_79 (not_79_out, i26);
  not not_80 (not_80_out, i30);
  not not_81 (not_81_out, i29);
  not not_82 (not_82_out, i27);
  not not_83 (not_83_out, i26);
  and and_1 (j, not_1_out, not_2_out, not_3_out, not_4_out, i27);
  and and_2 (and_2_out, not_6_out, not_7_out, not_8_out, not_9_out, not_10_out, i26);
  and and_3 (and_3_out, i28, i27, i26);
  and and_4 (and_4_out, not_11_out, not_12_out, i29, not_13_out, i27);
  and and_5 (and_5_out, i29, i28, i26);
  and and_6 (and_6_out, i30, i28, i26);
  and and_7 (and_7_out, i31, i28, i26);
  and and_8 (and_8_out, not_14_out, not_15_out);
  and and_9 (and_9_out, not_16_out, not_17_out, not_18_out, i28, not_19_out);
  and and_10 (and_10_out, not_20_out, i29, not_21_out, i26);
  and and_11 (and_11_out, i30, not_22_out, not_23_out);
  and and_12 (and_12_out, i31, not_24_out, not_25_out, i26);
  and and_13 (and_13_out, not_26_out, not_27_out, not_28_out, not_29_out, i26);
  and and_14 (and_14_out, not_30_out, i28, not_31_out);
  and and_15 (and_15_out, i28, i27, not_32_out);
  and and_16 (and_16_out, not_33_out, not_34_out, i29, i27, not_35_out);
  and and_17 (and_17_out, i29, i28, not_36_out);
  and and_18 (and_18_out, i30, i28, not_37_out);
  and and_19 (and_19_out, not_38_out, not_39_out);
  and and_20 (and_20_out, not_40_out, not_41_out, i29, not_42_out, not_43_out);
  and and_21 (and_21_out, i29, not_44_out, not_45_out);
  and and_22 (and_22_out, i30, not_46_out, not_47_out);
  and and_23 (and_23_out, i31, not_48_out, not_49_out);
  and and_24 (and_24_out, i31, not_50_out, not_51_out, i26);
  and and_25 (and_25_out, i31, not_52_out, not_53_out, i27, i26);
  and and_26 (and_26_out, i31, not_54_out, not_55_out, i28, not_56_out, not_57_out);
  and and_27 (and_27_out, not_58_out, not_59_out, not_60_out, not_61_out, i26);
  and and_28 (and_28_out, not_62_out, not_63_out, not_64_out, i28, not_65_out);
  and and_29 (and_29_out, not_67_out, not_68_out, i29, not_69_out);
  and and_30 (and_30_out, not_70_out, not_71_out, i29, not_72_out);
  and and_31 (and_31_out, i31, not_73_out, not_74_out, not_75_out, i27, i26);
  and and_32 (and_32_out, i31, not_76_out, not_77_out, i28, not_78_out, not_79_out);
  and and_33 (LBU, i31, not_80_out, not_81_out, i28, not_82_out, not_83_out);
  or or_1 (op3, and_2_out, and_3_out, and_4_out, and_5_out, and_6_out, and_7_out);
  or or_2 (op2, and_8_out, and_9_out, and_10_out, and_11_out, and_12_out);
  or or_3 (op1, and_13_out, and_14_out, and_15_out, and_16_out, and_17_out, and_18_out);
  or or_4 (op0, and_19_out, and_20_out, and_21_out, and_22_out, and_23_out, and_24_out);
  or or_5 (rw, and_25_out, and_26_out);
  or or_6 (eq, and_27_out, and_28_out);
  or or_7 (regwrite, and_29_out, and_30_out, and_31_out, and_32_out);

  assign rw2 = i29;
endmodule

module istWithFun (
  input  i5,
  input  i4,
  input  i3,
  input  i2,
  input  i1,
  input  i0,
  output op3,
  output op2,
  output op1,
  output op0,
  output j,
  output regwrite,
  output shift
);

  wire and_1_out, and_2_out, and_3_out, and_4_out, and_5_out, and_6_out, and_7_out, and_8_out, and_10_out,
       and_11_out, and_12_out, and_13_out, and_14_out, and_15_out, and_16_out, and_17_out, not_1_out,
       not_2_out, not_3_out, not_4_out, not_5_out, not_6_out, not_7_out, not_8_out, not_9_out, not_10_out,
       not_11_out, not_12_out, not_13_out, not_14_out, not_15_out, not_16_out, not_17_out, not_18_out,
       not_19_out, not_20_out, not_21_out, not_22_out, not_23_out, not_24_out, not_25_out, not_26_out,
       not_27_out, not_28_out, not_29_out, not_30_out, not_31_out, not_32_out, not_33_out, not_34_out,
       not_35_out, not_36_out, not_37_out, not_38_out, not_39_out, not_40_out, not_41_out, not_42_out,
       not_43_out, not_44_out, not_45_out;

  and and_1 (and_1_out, i2, i0);
  not not_1 (not_1_out, i4);
  not not_2 (not_2_out, i3);
  not not_3 (not_3_out, i2);
  not not_4 (not_4_out, i1);
  not not_5 (not_5_out, i3);
  not not_6 (not_6_out, i0);
  not not_7 (not_7_out, i0);
  not not_8 (not_8_out, i0);
  not not_9 (not_9_out, i2);
  not not_10 (not_10_out, i1);
  not not_11 (not_11_out, i0);
  not not_12 (not_12_out, i5);
  not not_13 (not_13_out, i4);
  not not_14 (not_14_out, i2);
  not not_15 (not_15_out, i1);
  not not_16 (not_16_out, i0);
  not not_17 (not_17_out, i4);
  not not_18 (not_18_out, i3);
  not not_19 (not_19_out, i2);
  not not_20 (not_20_out, i0);
  not not_21 (not_21_out, i5);
  not not_22 (not_22_out, i4);
  not not_23 (not_23_out, i3);
  not not_24 (not_24_out, i2);
  not not_25 (not_25_out, i4);
  not not_26 (not_26_out, i3);
  not not_27 (not_27_out, i0);
  not not_28 (not_28_out, i4);
  not not_29 (not_29_out, i3);
  not not_30 (not_30_out, i1);
  not not_31 (not_31_out, i4);
  not not_32 (not_32_out, i2);
  not not_33 (not_33_out, i5);
  not not_34 (not_34_out, i4);
  not not_35 (not_35_out, i3);
  not not_36 (not_36_out, i2);
  not not_37 (not_37_out, i0);
  not not_38 (not_38_out, i5);
  not not_39 (not_39_out, i4);
  not not_40 (not_40_out, i3);
  not not_41 (not_41_out, i2);
  not not_42 (not_42_out, i5);
  not not_43 (not_43_out, i4);
  not not_44 (not_44_out, i3);
  not not_45 (not_45_out, i0);
  or or_1 (op3, and_1_out, i3);
  and and_2 (and_2_out, i5, not_1_out, not_2_out, not_3_out, not_4_out);
  and and_3 (and_3_out, i5, not_5_out, not_6_out);
  and and_4 (and_4_out, i1, not_7_out);
  and and_5 (and_5_out, i2, not_8_out);
  and and_6 (and_6_out, i5, i1);
  and and_7 (and_7_out, not_9_out, i0);
  and and_8 (and_8_out, i5, not_10_out, not_11_out);
  and and_9 (j, not_12_out, not_13_out, i3, not_14_out, not_15_out, not_16_out);
  and and_10 (and_10_out, not_17_out, not_18_out, not_19_out, not_20_out);
  and and_11 (and_11_out, not_21_out, not_22_out, not_23_out, not_24_out, i1);
  and and_12 (and_12_out, not_25_out, not_26_out, i1, not_27_out);
  and and_13 (and_13_out, i5, not_28_out, not_29_out, not_30_out);
  and and_14 (and_14_out, i5, not_31_out, i3, not_32_out, i1);
  and and_15 (and_15_out, not_33_out, not_34_out, not_35_out, not_36_out, not_37_out);
  and and_16 (and_16_out, not_38_out, not_39_out, not_40_out, not_41_out, i1);
  and and_17 (and_17_out, not_42_out, not_43_out, not_44_out, i1, not_45_out);
  or or_2 (op2, and_2_out, and_3_out);
  or or_3 (op1, and_4_out, and_5_out, and_6_out);
  or or_4 (op0, and_7_out, i3, and_8_out);
  or or_5 (regwrite, and_10_out, and_11_out, and_12_out, and_13_out, and_14_out);
  or or_6 (shift, and_15_out, and_16_out, and_17_out);
endmodule

// Control
module Ist (
  input  [5:0] _5_0,
  input  [5:0] _31_26,
  output shift,
  output syscall,
  output [3:0] aluop,
  output Opcode,
  output [1:0] Branch,
  output memwrite,
  output regwrite,
  output memread,
  output [1:0] jump,
  output lbu,
  output bgez
);

  wire and_1_out, funcj, Funct_regwrite, Funct_shift, isop, istwithop_1_j, istwithop_1_j2, istwithop_1_lbu,
       istwithop_1_regwrite, istwithop_1_rw, istwithop_1_rw2, not_1_out, not_2_out, not_3_out, not_4_out,
       not_5_out, not_6_out, not_7_out, not_8_out, not_9_out;
  wire [3:0] Funct_op0, istwithop_1_op0;

  not not_1 (not_1_out, _5_0[5]);
  not not_2 (not_2_out, _5_0[4]);
  not not_3 (not_3_out, _5_0[1]);
  not not_4 (not_4_out, _5_0[0]);
  istWithOp istwithop_1 (
    .i31(_31_26[5]), .i30(_31_26[4]), .i29(_31_26[3]), .i28(_31_26[2]), .i27(_31_26[1]), .i26(_31_26[0]),
    .j(istwithop_1_j), .j2(istwithop_1_j2), .op3(istwithop_1_op0[3]), .op2(istwithop_1_op0[2]),
    .op1(istwithop_1_op0[1]), .op0(istwithop_1_op0[0]), .rw(istwithop_1_rw), .rw2(istwithop_1_rw2),
    .eq(Branch[1]), .eq2(Branch[0]), .regwrite(istwithop_1_regwrite), .LBU(istwithop_1_lbu));
  and and_1 (and_1_out, not_1_out, not_2_out, _5_0[3], not_3_out, not_4_out, _5_0[2]);
  istWithFun Funct (
    .i5(_5_0[5]), .i4(_5_0[4]), .i3(_5_0[3]), .i2(_5_0[2]), .i1(_5_0[1]), .i0(_5_0[0]), .op3(Funct_op0[3]),
    .op2(Funct_op0[2]), .op1(Funct_op0[1]), .op0(Funct_op0[0]), .j(funcj), .regwrite(Funct_regwrite),
    .shift(Funct_shift));
  or or_1 (isop, _31_26[0], _31_26[1], _31_26[2], _31_26[3], _31_26[4], _31_26[5]);
  not not_5 (not_5_out, istwithop_1_rw2);
  not not_6 (not_6_out, istwithop_1_j2);
  Multiplexer #(.enable("false")) multiplexer_1 (.in0(funcj), .in1(istwithop_1_j), .out(jump[0]), .sel(isop));
  not not_7 (not_7_out, isop);
  and and_2 (jump[1], istwithop_1_j, not_6_out);
  and and_3 (syscall, and_1_out, not_7_out);
  Multiplexer #(.width(4), .enable("false")) multiplexer_2 (
    .in0(Funct_op0), .in1(istwithop_1_op0), .out(aluop), .sel(isop));
  and and_4 (memwrite, istwithop_1_rw, istwithop_1_rw2);
  and and_5 (memread, istwithop_1_rw, not_5_out);
  not not_8 (not_8_out, isop);
  and and_6 (lbu, memread, istwithop_1_lbu);
  not not_9 (not_9_out, _31_26[2]);
  and and_7 (shift, not_8_out, Funct_shift);
  xor xor_1 (Opcode, Branch[1], isop);
  Multiplexer #(.enable("false")) multiplexer_3 (
    .in0(Funct_regwrite), .in1(istwithop_1_regwrite), .out(regwrite), .sel(isop));
  and and_8 (bgez, Branch[1], _31_26[0], not_9_out);
endmodule

module IFID (
  input  lock,
  input  [31:0] PC_1,
  input  [31:0] instruction,
  input  [1:0] which_int,
  input  int_trigger,
  input  [31:0] EPC,
  input  [31:0] IE,
  input  clk,
  input  rst,
  output [31:0] PC_out,
  output [31:0] instruction_out,
  output [1:0] int_num_out,
  output int_sig,
  output [31:0] EPC_out,
  output [31:0] IE_out
);

  wire d_ff_1_q, not_1_out;

  not not_1 (not_1_out, lock);
  Register #(.width(32)) register_1 (.D(PC_1), .en(not_1_out), .Q(PC_out), .clk(clk), .clr(d_ff_1_q));
  Register #(.width(32)) register_2 (.D(instruction), .en(not_1_out), .Q(instruction_out), .clk(clk), .clr(d_ff_1_q));
  Register #(.width(2)) register_3 (.D(which_int), .en(not_1_out), .Q(int_num_out), .clk(clk), .clr(d_ff_1_q));
  Register #(.width(1)) register_4 (.D(int_trigger), .en(not_1_out), .Q(int_sig), .clk(clk), .clr(d_ff_1_q));
  Register #(.width(32)) register_5 (.D(EPC), .en(not_1_out), .Q(EPC_out), .clk(clk));  // open: clr
  Register #(.width(32)) register_6 (.D(IE), .en(not_1_out), .Q(IE_out), .clk(clk), .clr(d_ff_1_q));
  D_Flip_Flop d_ff_1 (.clk(clk), .D(rst), .Q(d_ff_1_q), .en(not_1_out), .reset(d_ff_1_q));  // open: Qn, preset
endmodule

module Controller (
  input  [31:0] instruction,
  input  [31:0] IE_value,
  input  [31:0] EPC_value,
  output eret,
  output [31:0] instr_index,
  output [31:0] imm16_ext,
  output [31:0] shamt_ext,
  output [1:0] b_ins_label,
  output [3:0] aluop,
  output OporFun,
  output [4:0] R1_sel,
  output bgez,
  output [1:0] mem_label,
  output lbu,
  output [4:0] RW,
  output syscall,
  output shift,
  output We,
  output [1:0] j_label,
  output shift_op_judge,
  output [4:0] R2_sel,
  output mfc0,
  output mtc0,
  output CPR0,
  output [31:0] CPR_value
);

  wire and_1_out, and_3_out, comparator_1_eq, comparator_3_eq, comparator_4_eq, comparator_5_eq,
       comparator_6_eq, ist_1_regwrite, multiplexer_4_out, nop, not_1_out;
  wire [4:0] multiplexer_1_out, multiplexer_3_out, rs, rt, shift_jud;
  wire [4:1] rd;
  wire [5:0] ir_1__5_0, Opcode;
  wire [15:0] ir_1__0_15;
  wire [25:0] ir_1__25_0;

  nor nor_1 (shift_op_judge, shift_jud[0], shift_jud[1], shift_jud[2], shift_jud[3], shift_jud[4]);
  Comparator #(.width(6)) comparator_1 (.a(Opcode), .b(6'b010000), .eq(comparator_1_eq));  // open: gt, lt
  IR ir_1 (
    .\input (instruction), ._25_0(ir_1__25_0), ._26_31(Opcode), ._21_25(rs), ._16_20(rt),
    ._11_15({rd, CPR0}), ._0_15(ir_1__0_15), ._5_0(ir_1__5_0), ._6_10(shift_jud));
  Comparator #(.width(32)) comparator_2 (.a(instruction), .b({32{1'b0}}), .eq(nop));  // open: gt, lt
  and and_1 (and_1_out, comparator_1_eq, rs[4]);
  Multiplexer #(.width(5), .enable("false")) multiplexer_1 (
    .in0(rt), .in1(rs), .out(multiplexer_1_out), .sel(shift_op_judge));
  Multiplexer #(.width(5), .enable("false")) multiplexer_2 (
    .in0(rt), .in1(multiplexer_1_out), .out(R2_sel), .sel(shift));
  and and_2 (eret, and_1_out, comparator_3_eq);
  Comparator #(.width(6)) comparator_3 (.a(ir_1__5_0), .b(6'b011000), .eq(comparator_3_eq));  // open: gt, lt
  Ist ist_1 (
    ._5_0(ir_1__5_0), ._31_26(Opcode), .aluop(aluop), .Opcode(OporFun), .memwrite(mem_label[0]),
    .regwrite(ist_1_regwrite), .memread(mem_label[1]), .Branch(b_ins_label), .syscall(syscall),
    .shift(shift), .jump(j_label), .lbu(lbu), .bgez(bgez));
  assign imm16_ext = {{16{ir_1__0_15[15]}}, ir_1__0_15};  // Bit_Extender bit_extender_1
  Multiplexer #(.width(5), .enable("false")) multiplexer_3 (
    .in0({rd, CPR0}), .in1(rt), .out(multiplexer_3_out), .sel(OporFun));
  Multiplexer #(.enable("false")) multiplexer_4 (
    .in0(ist_1_regwrite), .in1(1'b1), .out(multiplexer_4_out), .sel(j_label[1]));
  assign instr_index = {{6{1'b0}}, ir_1__25_0};  // Bit_Extender bit_extender_2
  assign shamt_ext = {{27{1'b0}}, shift_jud};  // Bit_Extender bit_extender_3
  Multiplexer #(.width(5), .enable("false")) multiplexer_5 (.in0(rs), .in1(rt), .out(R1_sel), .sel(shift));
  Multiplexer #(.width(5), .enable("false")) multiplexer_6 (
    .in0(multiplexer_3_out), .in1({5{1'b1}}), .out(RW), .sel(j_label[1]));
  not not_1 (not_1_out, nop);
  Comparator #(.width(5)) comparator_4 (.a(rs), .b({5{1'b0}}), .eq(comparator_4_eq));  // open: gt, lt
  Comparator #(.width(6)) comparator_5 (.a(Opcode), .b(6'b010000), .eq(comparator_5_eq));  // open: gt, lt
  Comparator #(.width(5)) comparator_6 (.a(rs), .b(5'b00100), .eq(comparator_6_eq));  // open: gt, lt
  and and_3 (and_3_out, multiplexer_4_out, not_1_out);
  and and_4 (mfc0, comparator_4_eq, comparator_5_eq);
  or or_1 (We, and_3_out, mfc0);
  and and_5 (mtc0, comparator_5_eq, comparator_6_eq);
  Multiplexer #(.width(32), .enable("false")) multiplexer_7 (
    .in0(IE_value), .in1(EPC_value), .out(CPR_value), .sel(CPR0));

  // Other names for the same wires on the sheet: jump = j_label[0]; jal = j_label[1]; rd[0] = CPR0;
  //   shift_op_jud = shift_op_judge
endmodule

module IDEX (
  input  [31:0] PC_1,
  input  [31:0] jal_addr,
  input  [31:0] imm16_ext,
  input  [1:0] b_ins_label,
  input  CPR0,
  input  [31:0] CPR0_value,
  input  mfc0,
  input  mtc0,
  input  eret,
  input  [31:0] X_op,
  input  [31:0] Y_op,
  input  [31:0] write_value,
  input  [4:0] Rw,
  input  we,
  input  [3:0] aluop,
  input  [1:0] mem_label,
  input  syscall,
  input  int_trigger,
  input  [1:0] int_num,
  input  lbu,
  input  [1:0] jump,
  input  bgez,
  input  nop,
  input  clk,
  input  reset,
  output [31:0] PC_out,
  output [31:0] jal_addr_out,
  output [31:0] imm16_out,
  output [1:0] b_ins_out,
  output CPR0_2,
  output [31:0] CPR0_value_2,
  output mfc0_2,
  output mtc0_2,
  output eret_2,
  output [31:0] X,
  output [31:0] Y,
  output [31:0] ram_write,
  output [4:0] Rw_2,
  output we_2,
  output [3:0] aluop_2,
  output [1:0] mem_label_2,
  output syscall_2,
  output int_trigger_2,
  output [1:0] int_num_out,
  output lbu_2,
  output [1:0] jump_2,
  output bgez_2
);

  wire d_ff_1_q, register_5_q, register_7_q, register_8_q, register_9_q, register_14_q, register_17_q,
       register_18_q, register_20_q, register_22_q, register_23_q, undriven, undriven_2;
  wire [1:0] register_4_q, register_16_q, register_19_q, register_21_q;
  wire [3:0] register_15_q;
  wire [4:0] register_13_q;
  wire [31:0] register_1_q, register_2_q, register_3_q, register_6_q, register_10_q, register_11_q,
       register_12_q;

  Register #(.width(32)) register_1 (.D(PC_1), .en(1'b1), .Q(register_1_q), .clk(clk), .clr(d_ff_1_q));
  Register #(.width(32)) register_2 (.D(jal_addr), .en(1'b1), .Q(register_2_q), .clk(clk), .clr(d_ff_1_q));
  Register #(.width(32)) register_3 (.D(imm16_ext), .en(1'b1), .Q(register_3_q), .clk(clk), .clr(d_ff_1_q));
  Register #(.width(2)) register_4 (.D(b_ins_label), .en(1'b1), .Q(register_4_q), .clk(clk), .clr(d_ff_1_q));
  Register #(.width(1)) register_5 (.D(CPR0), .en(1'b1), .Q(register_5_q), .clk(clk), .clr(d_ff_1_q));
  Register #(.width(32)) register_6 (.D(CPR0_value), .en(1'b1), .Q(register_6_q), .clk(clk), .clr(d_ff_1_q));
  Register #(.width(1)) register_7 (.D(mfc0), .en(1'b1), .Q(register_7_q), .clk(clk), .clr(d_ff_1_q));
  Register #(.width(1)) register_8 (.D(mtc0), .en(1'b1), .Q(register_8_q), .clk(clk), .clr(d_ff_1_q));
  Register #(.width(1)) register_9 (.D(eret), .en(1'b1), .Q(register_9_q), .clk(clk), .clr(d_ff_1_q));
  Register #(.width(32)) register_10 (.D(X_op), .en(1'b1), .Q(register_10_q), .clk(clk), .clr(undriven));
  Register #(.width(32)) register_11 (.D(Y_op), .en(1'b1), .Q(register_11_q), .clk(clk), .clr(undriven_2));
  Register #(.width(32)) register_12 (.D(write_value), .en(1'b1), .Q(register_12_q), .clk(clk), .clr(d_ff_1_q));
  Register #(.width(5)) register_13 (.D(Rw), .en(1'b1), .Q(register_13_q), .clk(clk), .clr(d_ff_1_q));
  Register #(.width(1)) register_14 (.D(we), .en(1'b1), .Q(register_14_q), .clk(clk), .clr(d_ff_1_q));
  Register #(.width(4)) register_15 (.D(aluop), .en(1'b1), .Q(register_15_q), .clk(clk), .clr(d_ff_1_q));
  Register #(.width(2)) register_16 (.D(mem_label), .en(1'b1), .Q(register_16_q), .clk(clk), .clr(d_ff_1_q));
  Register #(.width(1)) register_17 (.D(syscall), .en(1'b1), .Q(register_17_q), .clk(clk), .clr(d_ff_1_q));
  Register #(.width(1)) register_18 (.D(int_trigger), .en(1'b1), .Q(register_18_q), .clk(clk), .clr(d_ff_1_q));
  Register #(.width(2)) register_19 (.D(int_num), .en(1'b1), .Q(register_19_q), .clk(clk), .clr(d_ff_1_q));
  Register #(.width(1)) register_20 (.D(lbu), .en(1'b1), .Q(register_20_q), .clk(clk), .clr(d_ff_1_q));
  Register #(.width(2)) register_21 (.D(jump), .en(1'b1), .Q(register_21_q), .clk(clk), .clr(d_ff_1_q));
  Register #(.width(1)) register_22 (.D(bgez), .en(1'b1), .Q(register_22_q), .clk(clk), .clr(d_ff_1_q));
  Register #(.width(1)) register_23 (.D(nop), .en(1'b1), .Q(register_23_q), .clk(clk), .clr(d_ff_1_q));
  D_Flip_Flop d_ff_1 (.clk(clk), .D(reset), .Q(d_ff_1_q));  // open: Qn, preset, en, reset
  Multiplexer #(.width(32), .enable("false")) multiplexer_1 (
    .in0(register_1_q), .in1({32{1'b0}}), .out(PC_out), .sel(register_23_q));
  Multiplexer #(.width(32), .enable("false")) multiplexer_2 (
    .in0(register_2_q), .in1({32{1'b0}}), .out(jal_addr_out), .sel(register_23_q));
  Multiplexer #(.width(32), .enable("false")) multiplexer_3 (
    .in0(register_3_q), .in1({32{1'b0}}), .out(imm16_out), .sel(register_23_q));
  Multiplexer #(.width(2), .enable("false")) multiplexer_4 (
    .in0(register_4_q), .in1(2'b00), .out(b_ins_out), .sel(register_23_q));
  Multiplexer #(.enable("false")) multiplexer_5 (.in0(register_5_q), .in1(1'b0), .out(CPR0_2), .sel(register_23_q));
  Multiplexer #(.width(32), .enable("false")) multiplexer_6 (
    .in0(register_6_q), .in1({32{1'b0}}), .out(CPR0_value_2), .sel(register_23_q));
  Multiplexer #(.enable("false")) multiplexer_7 (.in0(register_7_q), .in1(1'b0), .out(mfc0_2), .sel(register_23_q));
  Multiplexer #(.enable("false")) multiplexer_8 (.in0(register_8_q), .in1(1'b0), .out(mtc0_2), .sel(register_23_q));
  Multiplexer #(.enable("false")) multiplexer_9 (.in0(register_9_q), .in1(1'b0), .out(eret_2), .sel(register_23_q));
  Multiplexer #(.width(32), .enable("false")) multiplexer_10 (
    .in0(register_10_q), .in1({32{1'b0}}), .out(X), .sel(register_23_q));
  Multiplexer #(.width(32), .enable("false")) multiplexer_11 (
    .in0(register_11_q), .in1({32{1'b0}}), .out(Y), .sel(register_23_q));
  Multiplexer #(.width(32), .enable("false")) multiplexer_12 (
    .in0(register_12_q), .in1({32{1'b0}}), .out(ram_write), .sel(register_23_q));
  Multiplexer #(.width(5), .enable("false")) multiplexer_13 (
    .in0(register_13_q), .in1({5{1'b0}}), .out(Rw_2), .sel(register_23_q));
  Multiplexer #(.enable("false")) multiplexer_14 (.in0(register_14_q), .in1(1'b0), .out(we_2), .sel(register_23_q));
  Multiplexer #(.width(4), .enable("false")) multiplexer_15 (
    .in0(register_15_q), .in1(4'b0000), .out(aluop_2), .sel(register_23_q));
  Multiplexer #(.width(2), .enable("false")) multiplexer_16 (
    .in0(register_16_q), .in1(2'b00), .out(mem_label_2), .sel(register_23_q));
  Multiplexer #(.enable("false")) multiplexer_17 (
    .in0(register_17_q), .in1(1'b0), .out(syscall_2), .sel(register_23_q));
  Multiplexer #(.enable("false")) multiplexer_18 (
    .in0(register_18_q), .in1(1'b0), .out(int_trigger_2), .sel(register_23_q));
  Multiplexer #(.width(2), .enable("false")) multiplexer_19 (
    .in0(register_19_q), .in1(2'b00), .out(int_num_out), .sel(register_23_q));
  Multiplexer #(.enable("false")) multiplexer_20 (.in0(register_20_q), .in1(1'b0), .out(lbu_2), .sel(register_23_q));
  Multiplexer #(.width(2), .enable("false")) multiplexer_21 (
    .in0(register_21_q), .in1(2'b00), .out(jump_2), .sel(register_23_q));
  Multiplexer #(.enable("false")) multiplexer_22 (.in0(register_22_q), .in1(1'b0), .out(bgez_2), .sel(register_23_q));
endmodule

module EXMEM (
  input  [31:0] PC,
  input  [31:0] result,
  input  [31:0] write_value,
  input  [4:0] Rw,
  input  we,
  input  [1:0] mem_label,
  input  syscall,
  input  lbu,
  input  jal,
  input  clk,
  output [31:0] PC_2,
  output [31:0] result_2,
  output [31:0] ram_write,
  output [4:0] Rw_2,
  output we_2,
  output [1:0] mem_label_2,
  output syscall_2,
  output lbu_2,
  output jal_2
);

  Register #(.width(32)) register_1 (.D(PC), .en(1'b1), .Q(PC_2), .clk(clk));  // open: clr
  Register #(.width(32)) register_2 (.D(result), .en(1'b1), .Q(result_2), .clk(clk));  // open: clr
  Register #(.width(32)) register_3 (.D(write_value), .en(1'b1), .Q(ram_write), .clk(clk));  // open: clr
  Register #(.width(5)) register_4 (.D(Rw), .en(1'b1), .Q(Rw_2), .clk(clk));  // open: clr
  Register #(.width(1)) register_5 (.D(we), .en(1'b1), .Q(we_2), .clk(clk));  // open: clr
  Register #(.width(2)) register_6 (.D(mem_label), .en(1'b1), .Q(mem_label_2), .clk(clk));  // open: clr
  Register #(.width(1)) register_7 (.D(syscall), .en(1'b1), .Q(syscall_2), .clk(clk));  // open: clr
  Register #(.width(1)) register_8 (.D(lbu), .en(1'b1), .Q(lbu_2), .clk(clk));  // open: clr
  Register #(.width(1)) register_9 (.D(jal), .en(1'b1), .Q(jal_2), .clk(clk));  // open: clr
endmodule

module MEMWB (
  input  [31:0] sel1,
  input  [31:0] sel2,
  input  ld,
  input  [4:0] Rw,
  input  we,
  input  syscall,
  input  [31:0] PC_jal,
  input  jal,
  input  clk,
  output [31:0] sel1_2,
  output [31:0] sel2_2,
  output ld_2,
  output [4:0] Rw_2,
  output we_2,
  output syscall_2,
  output [31:0] PC_jal_2,
  output jal_2
);

  Register #(.width(32)) register_1 (.D(sel1), .en(1'b1), .Q(sel1_2), .clk(clk));  // open: clr
  Register #(.width(32)) register_2 (.D(sel2), .en(1'b1), .Q(sel2_2), .clk(clk));  // open: clr
  Register #(.width(1)) register_3 (.D(ld), .en(1'b1), .Q(ld_2), .clk(clk));  // open: clr
  Register #(.width(5)) register_4 (.D(Rw), .en(1'b1), .Q(Rw_2), .clk(clk));  // open: clr
  Register #(.width(1)) register_5 (.D(we), .en(1'b1), .Q(we_2), .clk(clk));  // open: clr
  Register #(.width(1)) register_6 (.D(syscall), .en(1'b1), .Q(syscall_2), .clk(clk));  // open: clr
  Register #(.width(32)) register_7 (.D(PC_jal), .en(1'b1), .Q(PC_jal_2), .clk(clk));  // open: clr
  Register #(.width(1)) register_8 (.D(jal), .en(1'b1), .Q(jal_2), .clk(clk));  // open: clr
endmodule

module Redirection (
  input  ID_mtc0,
  input  EX_load,
  input  ID_OporFun,
  input  ID_shift,
  input  [4:0] ID_R2,
  input  [4:0] ID_R1,
  input  [4:0] EX_RW,
  input  EX_We,
  input  [1:0] ID_mem,
  input  [4:0] MEM_RW,
  input  MEM_We,
  output lock,
  output IDMEMinter,
  output [1:0] Red_R1,
  output [1:0] Red_R2
);

  wire and_1_out, and_2_out, and_5_out, and_6_out, comparator_1_eq, comparator_2_eq, comparator_3_eq,
       comparator_4_eq, nor_1_out, not_1_out, not_2_out, or_1_out, or_2_out, or_3_out, or_4_out;

  nor nor_1 (nor_1_out, ID_OporFun, ID_shift);
  Comparator #(.width(5), .mode("unsigned")) comparator_1 (.a(ID_R2), .b(EX_RW), .eq(comparator_1_eq));  // open: gt, lt
  Comparator #(.width(5), .mode("unsigned")) comparator_2 (.a(ID_R1), .b(EX_RW), .eq(comparator_2_eq));  // open: gt, lt
  and and_1 (and_1_out, nor_1_out, comparator_1_eq);
  or or_1 (or_1_out, ID_mem[0], nor_1_out);
  Comparator #(.width(5), .mode("unsigned")) comparator_3 (
    .a(ID_R2), .b(MEM_RW), .eq(comparator_3_eq));  // open: gt, lt
  Comparator #(.width(5), .mode("unsigned")) comparator_4 (
    .a(ID_R1), .b(MEM_RW), .eq(comparator_4_eq));  // open: gt, lt
  or or_2 (or_2_out, ID_mtc0, and_1_out);
  not not_1 (not_1_out, EX_load);
  and and_2 (and_2_out, or_1_out, comparator_3_eq);
  and and_3 (Red_R1[0], not_1_out, comparator_2_eq, EX_We);
  or or_3 (or_3_out, and_1_out, comparator_2_eq);
  or or_4 (or_4_out, and_2_out, comparator_4_eq);
  and and_4 (Red_R2[0], not_1_out, or_2_out, EX_We);
  and and_5 (and_5_out, or_3_out, EX_We);
  and and_6 (and_6_out, or_4_out, MEM_We);
  and and_7 (Red_R2[1], and_2_out, MEM_We);
  and and_8 (Red_R1[1], comparator_4_eq, MEM_We);
  // NOT_Gate not_2 has open pins: in=open, out=not_2_out
  and and_9 (lock, EX_load, and_5_out);
  and and_10 (IDMEMinter, not_2_out, and_6_out);

  // Other names for the same wires on the sheet: sw = ID_mem[0]; EX_R1_Red = Red_R1[0]; MEM_R1_Red = Red_R1[1];
  //   EX_R2_Red = Red_R2[0]; MEM_R2_Red = Red_R2[1]
endmodule

module interrupt (
  input  _1,
  input  _2,
  input  _3,
  input  clk,
  input  reg_jud,
  input  ex_mtc,
  input  ex_int_tri,
  input  ex_eret,
  input  [31:0] EX_PC_next,
  input  [31:0] EX_rt,
  output [1:0] lock_value,
  output [1:0] which_int,
  output int_trigger,
  output [31:0] EPC,
  output [31:0] IE
);

  wire \_1号中断等待指示 , \_2号中断等待指示 , \_3号中断等待指示 , and_1_out, and_2_out, and_3_out, and_4_out, and_5_out,
       and_6_out, and_7_out, and_8_out, and_14_out, and_15_out, bit_extender_1_out, clock_1_out, d_ff_1_q,
       d_ff_2_q, d_ff_3_q, decoder_1_out1, decoder_1_out2, decoder_1_out3, IE_value, not_1_out, not_2_out,
       not_3_out, not_4_out, one, or_1_out, or_2_out, or_3_out, or_4_out, or_5_out, or_6_out, or_7_out,
       or_8_out, or_9_out, or_10_out, or_11_out, register_1_q, register_2_q, register_3_q, reset1, reset2,
       reset3, three, two, undriven, undriven_2;
  wire [31:0] alu_1_result, multiplexer_1_out;

  LED \_1号中断等待指示灯  (.in(or_2_out));
  or or_1 (or_1_out, lock_value[1], lock_value[0]);
  and and_1 (and_1_out, lock_value[1], lock_value[0]);
  or or_2 (or_2_out, one, d_ff_1_q);
  LED \_2号中断等待指示灯  (.in(or_3_out));
  or or_3 (or_3_out, two, d_ff_2_q);
  LED \_3号中断等待指示灯  (.in(or_4_out));
  or or_4 (or_4_out, three, d_ff_3_q);
  Register #(.width(1)) register_1 (.D(or_1_out), .Q(register_1_q), .clk(clk));  // open: en, clr
  Register #(.width(1)) register_2 (.D(lock_value[1]), .Q(register_2_q), .clk(clk));  // open: en, clr
  Register #(.width(1)) register_3 (.D(and_1_out), .Q(register_3_q), .clk(clk));  // open: en, clr
  LED u__1 (.in(\_1号中断等待指示 ));
  LED u__2 (.in(\_2号中断等待指示 ));
  LED u__3 (.in(\_3号中断等待指示 ));
  D_Flip_Flop d_ff_1 (.clk(_1), .D(1'b1), .Q(d_ff_1_q), .reset(one));  // open: Qn, preset, en
  D_Flip_Flop d_ff_2 (.clk(_2), .D(1'b1), .Q(d_ff_2_q), .reset(two));  // open: Qn, preset, en
  D_Flip_Flop d_ff_3 (.clk(_3), .D(1'b1), .Q(d_ff_3_q), .reset(three));  // open: Qn, preset, en
  not not_1 (not_1_out, register_1_q);
  not not_2 (not_2_out, register_2_q);
  not not_3 (not_3_out, register_3_q);
  or or_5 (or_5_out, d_ff_1_q, one);
  and and_2 (and_2_out, or_5_out, ~reset1);  // AND_Gate
  or or_6 (or_6_out, d_ff_2_q, two);
  or or_7 (or_7_out, d_ff_3_q, three);
  and and_3 (and_3_out, or_7_out, ~reset3);  // AND_Gate
  and and_4 (and_4_out, one, not_1_out);
  and and_5 (and_5_out, two, not_2_out);
  and and_6 (and_6_out, three, not_3_out);
  D_Flip_Flop IR1 (.clk(clk), .D(and_2_out), .Q(one));  // open: Qn, preset, en, reset
  and and_7 (and_7_out, or_6_out, ~reset2);  // AND_Gate
  D_Flip_Flop IR2 (.clk(clk), .D(and_3_out), .Q(three), .preset(undriven), .en(undriven));  // open: Qn, reset
  D_Flip_Flop IR2_2 (.clk(clk), .D(and_7_out), .Q(two), .preset(undriven_2), .en(undriven_2));  // open: Qn, reset
  Priority_Encoder #(.select(2)) priority_encoder_1 (
    .in0(1'b1), .in1(and_4_out), .in2(and_5_out), .in3(and_6_out), .out(which_int), .en_in(1'b1));  // open: gs, en_out
  or or_8 (or_8_out, and_4_out, and_5_out, and_6_out);
  and and_8 (and_8_out, ~IE_value, or_8_out);  // AND_Gate
  or or_9 (or_9_out, which_int[1], which_int[0]);
  // AND_Gate and_9 has open pins: in0=or_9_out, in1=or_8_out, out=open
  and and_10 (int_trigger, or_9_out, and_8_out);
  or or_10 (or_10_out, int_trigger, ex_eret);
  Register #(.width(2)) cur (.D(which_int), .en(or_10_out), .Q(lock_value), .clk(clk));  // open: clr
  and and_11 (reset1, int_trigger, decoder_1_out1);
  ALU alu_1 (
    .AluOP(4'b0110), .X(EX_PC_next), .Result(alu_1_result), .Y(32'h1));  // open: Equal, Signed_Overflow, Result_2, UnSigned_Overflow
  Decoder #(.select(2)) decoder_1 (
    .out1(decoder_1_out1), .out2(decoder_1_out2), .out3(decoder_1_out3), .sel(lock_value));  // open: out0, en
  and and_12 (reset2, int_trigger, decoder_1_out2);
  and and_13 (reset3, int_trigger, decoder_1_out3);
  or or_11 (or_11_out, ex_int_tri, and_14_out);
  Clock clock_1 (.out(clock_1_out));
  and and_14 (and_14_out, ex_mtc, reg_jud);
  Multiplexer #(.width(32), .enable("false")) multiplexer_1 (
    .in0(alu_1_result), .in1(EX_rt), .out(multiplexer_1_out), .sel(and_14_out));
  and and_15 (and_15_out, ex_mtc, not_4_out);
  Bit_Extender #(.in_width(32), .out_width(1)) bit_extender_1 (.in(EX_rt), .out(bit_extender_1_out));
  not not_4 (not_4_out, reg_jud);
  Register #(.width(32)) EPCache (.D(multiplexer_1_out), .en(or_11_out), .Q(EPC), .clk(clk));  // open: clr
  Register #(.width(1)) u_IE (.D(bit_extender_1_out), .en(and_15_out), .Q(IE_value), .clk(clk));  // open: clr
  assign IE = {{31{1'b0}}, IE_value};  // Bit_Extender bit_extender_2

  // Other names for the same wires on the sheet: _1号中断 = _1; _2号中断 = _2; _3号中断 = _3; eret = ex_eret

  // Notes on the sheet:
  //   Reset 
  //   Reset 
  //   Reset 
endmodule
